// Digital circuit datapath_completo.dig as structural Verilog
module datapath_completo (
  input  ALU_SR,
  input  ALU_TMPS,
  input  Op1,
  input  Op0,
  input  compl_1,
  input  cin,
  input  IB_3,
  input  IB_2,
  input  IB_1,
  input  IB_0,
  input  IB_TMPE,
  input  SR_IB,
  input  TMPS_IB,
  input  R1_IB,
  input  IB_R1,
  input  R0_IB,
  input  IB_R0,
  output S_3,
  output S_2,
  output S_1,
  output S_0
);

  wire alu4_1_p5, alu4_1_p6, alu4_1_p8, alu4_1_p10, alu4_1_p17, alu4_1_p18, alu4_1_p19, alu4_1_p20;

  // alu4 alu4_1: pin names not known; wires that end beside it: Op1, Op0, compl_1, cin, alu4_1_p5, alu4_1_p6, S_3, alu4_1_p8, S_2, alu4_1_p10, S_1, IB_3, S_0, IB_2, IB_1, IB_0, alu4_1_p17, alu4_1_p18, alu4_1_p19, alu4_1_p20
  // reg4 reg4_1: pin names not known; wires that end beside it: alu4_1_p5, IB_TMPE, alu4_1_p6, IB_3, alu4_1_p8, IB_2, alu4_1_p10, IB_1, IB_0
  // reg4_e_s reg4_e_s_1: pin names not known; wires that end beside it: ALU_TMPS, TMPS_IB, S_3, S_2, S_1, S_0, IB_3, IB_2, IB_1, IB_0
  // reg4_e_s reg4_e_s_2: pin names not known; wires that end beside it: ALU_SR, SR_IB, alu4_1_p17, alu4_1_p18, alu4_1_p19, alu4_1_p20, IB_3, IB_2, IB_1, IB_0
  reg4_tri reg4_tri_1 (.Write(IB_R0), .Read(R0_IB), .d_3(IB_3), .d_2(IB_2), .d_1(IB_1), .d_0(IB_0));
  reg4_tri reg4_tri_2 (.Write(IB_R1), .Read(R1_IB), .d_3(IB_3), .d_2(IB_2), .d_1(IB_1), .d_0(IB_0));
endmodule
