// Digital circuit Eje2-circuito1.dig as structural Verilog
module Eje2_circuito1 (
  input  e_2,
  input  e_1,
  input  e_0,
  output out_4
);

  // And and_1 has open pins: In_1=e_2, In_2=e_1, out=open
  // XOr xor_1 has open pins: In_1=e_1, In_2=e_0, out=open
  // Or or_1 has open pins: In_1=open, In_2=open, out=out_4
endmodule
