// Digital circuit Eje2_circuito2.dig as structural Verilog
module Eje2_circuito2 (
  input  e2,
  input  e1,
  input  e0,
  output s
);

  wire nor_1_out;

  nor nor_1 (nor_1_out, e1, e0);
  and and_1 (s, e2, nor_1_out);
endmodule
